// Logisim project olaf2.circ as structural Verilog: 6 circuits, main circuit main
module main (
  input  RST
);

  wire CLK_out, cpu_1_get, cpu_1_out, cpu_1_ram_str, cpu_1_rst_out, not_1_out, RST_out, undriven;
  wire [6:0] keyboard_1_data;
  wire [15:0] bit_extender_1_out, cpu_1_get_2, cpu_1_prnt_data, cpu_1_ram_store, cpu_1_sp,
       pull_resistor_2_node;
  wire [23:0] rom_1_data;

  Clock CLK (.out(CLK_out));
  or u_RST (RST_out, cpu_1_rst_out, RST);
  Pull_Resistor pull_resistor_1 (.node(RST));
  CPU cpu_1 (
    .CLK(CLK_out), .RST_IN(RST), .OPCODE(rom_1_data), .GET_2(cpu_1_get_2[0]), .RST_OUT(cpu_1_rst_out),
    .PRNT_DATA(cpu_1_prnt_data), .IN(bit_extender_1_out), .OUT(cpu_1_out), .GET(cpu_1_get), .SP(cpu_1_sp),
    .RAM_STORE(cpu_1_ram_store), .RAM_LOAD(pull_resistor_2_node), .RAM_STR(cpu_1_ram_str), .in_3(undriven));
  ROM #(.addrWidth(16), .dataWidth(24)) rom_1 (.addr(cpu_1_get_2), .data(rom_1_data), .sel(1'b1));
  Pull_Resistor pull_resistor_2 (.node(pull_resistor_2_node));
  TTY #(.rows(16), .cols(64)) tty_1 (.data(cpu_1_prnt_data[6:0]), .clk(CLK_out), .we(cpu_1_out), .clr(RST_out));
  Keyboard #(.buflen(256)) keyboard_1 (
    .clk(not_1_out), .re(cpu_1_get), .clr(RST_out), .data(keyboard_1_data));  // open: avail
  not not_1 (not_1_out, CLK_out);
  not not_2 (not_1_out, CLK_out);
  assign bit_extender_1_out = {{9{1'b0}}, keyboard_1_data};  // Bit_Extender bit_extender_1
  // Pins of 1 and 16 bits meet at cpu_1_get_2

  // Notes on the sheet:
  //   contents of rom_1 (hex, n*v repeats v):
  //   1d11 5c 7c 9c bc 3c fc 3d 621 1c f 722 10 1d 3d 3e2 1e 1d fc 3d 721 10 1d 3d bd 9d 7d 5d 1e 1081b 9a
  //   cd1b a19 79a cd1b 799a b51b 799a cd1b 4019 9a cd1b 2319 2019 f99a b51b f99a 63ba d81b 10c 5812 f99a
  //   5cba d81b 10c 5d12 f99a 6cba d81b 10c 5c12 f99a 53ba d81b 10c 5a12 f99a 59ba d81b 10c 5f12 f99a 72ba
  //   d81b 10c 6112 f93a 2f 2c 5712 f99a cd1b 3a19 2019 329a cd1b a19 2511 7a1b 2511 821b 2511 751b 631b
  //   2511 8b1b 2511 7c1b 2511 11b 5a 1561b e 20c d 7312 5c 9d 14e1b 1c 9d cd1b a19 141 6511 111b 1e 6219
  //   7919 6219 a19 1d11 c19 1e 11b 799a cd1b a19 111b 1e 11b 189a cd1b 1799a b51b 1799a 10f1b 111b 1e 11b
  //   189a cd1b 1799a b51b 1799a 1241b ffff0c 9a12 1799a cd1b 299a cd1b a19 1e 449a cd1b 111b 1e 3e19 9c
  //   2799a b51b 9d 2119 16*0 1e 9c 3d 1a 78 6c b812 86c c412 19 a6c ca12 70 121 101 b811 c b812 122 102
  //   19 b811 7a 70 1e 11b 9c 3d 6f 6c d612 19 121 d011 111b 1e 9c 3d f 181 bc 3d 4f 1a1 e 20c d e913 c
  //   e712 d811 11a eb11 1a eb11 1e 9c bc 9c 3d f bc 3d 10 c f912 181 1a1 ee11 bd 9d 1e 9c 11a 9c 3d 4f 4c
  //   10612 101 181 fe11 9d 1e 2843a 4861a 10 2853a 13861a 10 1e 11b 2843a af ec1b 2833a 8f 1621b 1c 3d b0
  //   2843a 8f fc1b e 401 d 2843a 10 1591b 111b 1e 11b 12e1b ffff0c 9e1b 12c12 1c 9d 1621b 111b 1e 11b 9c
  //   bd 5a 1561b e 20c d 14712 5c 9d 14e1b 1c 9d d81b e 20c d 14412 a19 141 6511 5c 1d 14811 ffff1a 111b
  //   1e 9c 1d 101 1e 1621b 1c 3d f 1e 1621b 101 1e 2833a f 1e 1c 1c 9d 1561b 101 2833a 10 1d 1e 283 28681
  //   9c 1d 1e
endmodule

module ALU (
  input  [15:0] SOURCE,
  input  [15:0] DEST,
  input  ADD,
  input  MUL,
  input  MUL_2,
  input  DIV,
  input  SHL,
  input  SHR,
  input  NOT,
  input  AND,
  input  OR,
  input  XOR,
  output ZERO,
  output CARRY,
  output BORROW,
  output [15:0] OUT,
  output [15:0] MOD,
  output ALU_USED
);

  wire not_2_out, not_3_out, not_4_out, not_5_out, not_6_out, not_7_out, not_8_out, not_9_out, not_10_out,
       not_11_out, not_12_out, not_13_out, not_14_out, not_15_out, not_16_out, not_17_out;
  wire [3:0] pull_resistor_4_node, pull_resistor_6_node;
  wire [15:0] adder_1_out, and_1_out, controlled_buffer_1_out, controlled_buffer_2_out,
       controlled_buffer_3_out, controlled_buffer_4_out, controlled_buffer_5_out, controlled_buffer_6_out,
       controlled_buffer_7_out, controlled_buffer_8_out, controlled_buffer_11_out, controlled_buffer_14_out,
       controlled_buffer_15_out, controlled_buffer_16_out, controlled_buffer_17_out, divider_1_out,
       multiplier_1_out, not_1_out, or_2_out, pull_resistor_3_node, pull_resistor_7_node,
       pull_resistor_12_node, pull_resistor_13_node, shifter_1_out, shifter_2_out, subtractor_1_out,
       xor_1_out;

  or or_1 (ALU_USED, ADD, MUL, MUL_2, DIV, SHL, SHR, NOT, AND, OR, XOR);
  assign controlled_buffer_1_out = ADD ? SOURCE : 16'bz;  // Controlled_Buffer controlled_buffer_1
  assign controlled_buffer_2_out = ADD ? DEST : 16'bz;  // Controlled_Buffer controlled_buffer_2
  assign controlled_buffer_3_out = MUL ? SOURCE : 16'bz;  // Controlled_Buffer controlled_buffer_3
  Pull_Resistor pull_resistor_1 (.node(controlled_buffer_3_out));
  assign controlled_buffer_4_out = MUL ? DEST : 16'bz;  // Controlled_Buffer controlled_buffer_4
  Pull_Resistor pull_resistor_2 (.node(controlled_buffer_4_out));
  assign controlled_buffer_5_out = MUL_2 ? SOURCE : 16'bz;  // Controlled_Buffer controlled_buffer_5
  assign controlled_buffer_6_out = MUL_2 ? DEST : 16'bz;  // Controlled_Buffer controlled_buffer_6
  assign controlled_buffer_7_out = DIV ? SOURCE : 16'bz;  // Controlled_Buffer controlled_buffer_7
  assign controlled_buffer_8_out = DIV ? DEST : 16'bz;  // Controlled_Buffer controlled_buffer_8
  Pull_Resistor pull_resistor_3 (.node(pull_resistor_3_node));
  assign pull_resistor_3_node = SHL ? SOURCE : 16'bz;  // Controlled_Buffer controlled_buffer_9
  Pull_Resistor pull_resistor_4 (.node(pull_resistor_4_node));
  assign pull_resistor_4_node = SHL ? DEST[3:0] : 4'bz;  // Controlled_Buffer controlled_buffer_10
  assign controlled_buffer_11_out = SHR ? SOURCE : 16'bz;  // Controlled_Buffer controlled_buffer_11
  Pull_Resistor pull_resistor_5 (.node(controlled_buffer_11_out));
  Pull_Resistor pull_resistor_6 (.node(pull_resistor_6_node));
  assign pull_resistor_6_node = SHR ? DEST[3:0] : 4'bz;  // Controlled_Buffer controlled_buffer_12
  Pull_Resistor #(.pull(1)) pull_resistor_7 (.node(pull_resistor_7_node));
  assign pull_resistor_7_node = NOT ? SOURCE : 16'bz;  // Controlled_Buffer controlled_buffer_13
  assign controlled_buffer_14_out = AND ? SOURCE : 16'bz;  // Controlled_Buffer controlled_buffer_14
  Pull_Resistor pull_resistor_8 (.node(controlled_buffer_14_out));
  assign controlled_buffer_15_out = AND ? DEST : 16'bz;  // Controlled_Buffer controlled_buffer_15
  Pull_Resistor pull_resistor_9 (.node(controlled_buffer_15_out));
  assign controlled_buffer_16_out = OR ? SOURCE : 16'bz;  // Controlled_Buffer controlled_buffer_16
  Pull_Resistor pull_resistor_10 (.node(controlled_buffer_16_out));
  assign controlled_buffer_17_out = OR ? DEST : 16'bz;  // Controlled_Buffer controlled_buffer_17
  Pull_Resistor pull_resistor_11 (.node(controlled_buffer_17_out));
  Pull_Resistor pull_resistor_12 (.node(pull_resistor_12_node));
  assign pull_resistor_12_node = XOR ? SOURCE : 16'bz;  // Controlled_Buffer controlled_buffer_18
  Pull_Resistor pull_resistor_13 (.node(pull_resistor_13_node));
  assign pull_resistor_13_node = XOR ? DEST : 16'bz;  // Controlled_Buffer controlled_buffer_19
  Adder #(.width(16)) adder_1 (
    .a(controlled_buffer_1_out), .b(controlled_buffer_2_out), .out(adder_1_out), .cout(CARRY));  // open: cin
  Subtractor #(.width(16)) subtractor_1 (
    .a(controlled_buffer_3_out), .b(controlled_buffer_4_out), .out(subtractor_1_out), .bin(1'b0),
    .bout(BORROW));
  Multiplier #(.width(16)) multiplier_1 (
    .a(controlled_buffer_5_out), .b(controlled_buffer_6_out), .out(multiplier_1_out), .cin(16'h1));  // open: cout
  Divider #(.width(16)) divider_1 (
    .a(controlled_buffer_7_out), .b(controlled_buffer_8_out), .out(divider_1_out), .upper({16{1'b0}}),
    .rem(MOD));
  Shifter #(.width(16)) shifter_1 (.in(pull_resistor_3_node), .\dist (pull_resistor_4_node), .out(shifter_1_out));
  Shifter #(.width(16), .shift("lr")) shifter_2 (
    .in(controlled_buffer_11_out), .\dist (pull_resistor_6_node), .out(shifter_2_out));
  assign not_1_out = ~pull_resistor_7_node;  // NOT_Gate not_1, 16 bits wide
  assign and_1_out = controlled_buffer_14_out & controlled_buffer_15_out;  // AND_Gate and_1, 16 bits wide
  assign or_2_out = controlled_buffer_16_out | controlled_buffer_17_out;  // OR_Gate or_2, 16 bits wide
  assign xor_1_out = pull_resistor_12_node ^ pull_resistor_13_node;  // XOR_Gate xor_1, 16 bits wide
  Pull_Resistor pull_resistor_14 (.node(adder_1_out));
  Pull_Resistor pull_resistor_15 (.node(multiplier_1_out));
  Pull_Resistor pull_resistor_16 (.node(divider_1_out));
  Pull_Resistor pull_resistor_17 (.node(shifter_1_out));
  Pull_Resistor pull_resistor_18 ();  // open: node
  Pull_Resistor pull_resistor_19 (.node(not_1_out));
  Pull_Resistor pull_resistor_20 (.node(and_1_out));
  Pull_Resistor pull_resistor_21 (.node(or_2_out));
  Pull_Resistor pull_resistor_22 (.node(xor_1_out));
  Pull_Resistor pull_resistor_23 (.node(CARRY));
  Pull_Resistor pull_resistor_24 (.node(BORROW));
  ExactlyOne xor_2[15:0] (
    .out(OUT), .in0(adder_1_out), .in1(subtractor_1_out), .in2(multiplier_1_out), .in3(divider_1_out),
    .in4(shifter_1_out), .in5(shifter_2_out), .in6(not_1_out), .in7(and_1_out), .in8(or_2_out),
    .in9(xor_1_out));
  Pull_Resistor pull_resistor_25 (.node(MOD));
  Pull_Resistor pull_resistor_26 (.node(OUT));
  not not_2 (not_2_out, OUT[0]);
  not not_3 (not_3_out, OUT[1]);
  not not_4 (not_4_out, OUT[2]);
  not not_5 (not_5_out, OUT[3]);
  not not_6 (not_6_out, OUT[4]);
  not not_7 (not_7_out, OUT[5]);
  not not_8 (not_8_out, OUT[6]);
  not not_9 (not_9_out, OUT[7]);
  not not_10 (not_10_out, OUT[8]);
  not not_11 (not_11_out, OUT[9]);
  not not_12 (not_12_out, OUT[10]);
  not not_13 (not_13_out, OUT[11]);
  not not_14 (not_14_out, OUT[12]);
  not not_15 (not_15_out, OUT[13]);
  not not_16 (not_16_out, OUT[14]);
  not not_17 (not_17_out, OUT[15]);
  and and_2 (ZERO, not_2_out, not_3_out, not_4_out, not_5_out, not_6_out, not_7_out, not_8_out, not_9_out, not_10_out, not_11_out, not_12_out, not_13_out, not_14_out, not_15_out, not_16_out, not_17_out, 1'b1);
endmodule

module CPU (
  input  [15:0] IN,
  input  CLK,
  input  in_3,
  input  RST_IN,
  input  [23:0] OPCODE,
  input  [15:0] RAM_LOAD,
  output GET,
  output OUT,
  output [15:0] PRNT_DATA,
  output RST_OUT,
  output RAM_LD,
  output RAM_STR,
  output [15:0] RAM_STORE,
  output GET_2,
  output [15:0] SP
);

  wire alu_1_alu_used, alu_1_borrow, alu_1_carry, alu_1_zero, controlled_buffer_2_out, decoder_1_out1,
       decoder_1_out2, decoder_1_out3, decoder_1_out4, decoder_1_out5, decoder_1_out6, decoder_1_out7,
       decoder_1_out8, decoder_1_out9, decoder_1_out10, decoder_1_out11, decoder_1_out12, decoder_1_out13,
       decoder_1_out14, decoder_1_out15, decoder_1_out16, decoder_1_out17, decoder_1_out18, decoder_1_out19,
       decoder_1_out20, decoder_1_out21, decoder_1_out22, decoder_1_out23, decoder_1_out25, decoder_1_out26,
       decoder_1_out27, decoder_1_out28, decoder_1_out29, decoder_1_out30, DIV_out, flags_1_jmp_out,
       flags_1_mod, HAS_VALLUE_out, i_o_1_prnt, JMP_out, MOV_2_out, MOV_out, nor_1_out, not_1_out, not_2_out,
       not_3_out, not_4_out, not_5_out, PSH_out, RST_2_out, RST_out_2, SUB_out;
  wire [2:0] flags_1_ip_reg, i_o_1_data_reg, REG_out;
  wire [15:0] alu_1_mod, alu_1_out, controlled_buffer_1_out, controlled_buffer_3_out,
       controlled_buffer_4_out, controlled_buffer_7_out, controlled_buffer_8_out, controlled_buffer_9_out,
       controlled_buffer_10_out, DST_out, i_o_1__in, or_1_out, pull_resistor_4_node, pull_resistor_6_node,
       pull_resistor_7_node, regs_1_out_10, regs_1_rb, regs_1_rc, regs_1_rdi, regs_1_rsi, regs_1_sp,
       undriven, VAL_out;
  wire [15:1] regs_1_rc_2;

  Decoder #(.select(5), .enable("false")) decoder_1 (
    .out1(decoder_1_out1), .out2(decoder_1_out2), .out3(decoder_1_out3), .out4(decoder_1_out4),
    .out5(decoder_1_out5), .out6(decoder_1_out6), .out7(decoder_1_out7), .out8(decoder_1_out8),
    .out9(decoder_1_out9), .out10(decoder_1_out10), .out11(decoder_1_out11), .out12(decoder_1_out12),
    .out13(decoder_1_out13), .out14(decoder_1_out14), .out15(decoder_1_out15), .out16(decoder_1_out16),
    .out17(decoder_1_out17), .out18(decoder_1_out18), .out19(decoder_1_out19), .out20(decoder_1_out20),
    .out21(decoder_1_out21), .out22(decoder_1_out22), .out23(decoder_1_out23), .out24(GET),
    .out25(decoder_1_out25), .out26(decoder_1_out26), .out27(decoder_1_out27), .out28(decoder_1_out28),
    .out29(decoder_1_out29), .out30(decoder_1_out30), .out31(RST_OUT), .sel(OPCODE[4:0]));  // open: out0
  or RST (RST_out_2, RST_OUT, RST_IN);
  Pull_Resistor pull_resistor_1 (.node(RAM_LOAD));
  or SUB (SUB_out, decoder_1_out2, decoder_1_out12);
  or JMP (JMP_out, decoder_1_out17, decoder_1_out30, decoder_1_out27);
  or PSH (PSH_out, decoder_1_out27, decoder_1_out28);
  assign REG_out = flags_1_ip_reg | i_o_1_data_reg | OPCODE[7:5];  // OR_Gate REG, 3 bits wide
  assign controlled_buffer_1_out = RST_2_out ? OPCODE[23:8] : 16'bz;  // Controlled_Buffer controlled_buffer_1
  Pull_Resistor pull_resistor_2 (.node(controlled_buffer_1_out));
  or RST_2 (RST_2_out, decoder_1_out26, flags_1_jmp_out);
  or HAS_VALLUE (HAS_VALLUE_out, OPCODE[8], OPCODE[9], OPCODE[10], OPCODE[11], OPCODE[12], OPCODE[13], OPCODE[14], OPCODE[15], 1'b0);
  FLAGS flags_1 (
    .JEQ_2(decoder_1_out18), .JNE(decoder_1_out19), .JST(decoder_1_out21), .JLE_2(decoder_1_out23),
    .BORROW(alu_1_borrow), .ZERO(alu_1_zero), .IP_REG(flags_1_ip_reg), .JMP_OUT(flags_1_jmp_out),
    .TEST(decoder_1_out12), .CLK_2(CLK), .CARRY_2(alu_1_carry), .MOD(flags_1_mod), .CHDC(decoder_1_out13),
    .JST_2(decoder_1_out14));
  or MOV (MOV_out, decoder_1_out26, flags_1_jmp_out, decoder_1_out15, MOV_2_out, GET);
  assign VAL_out = controlled_buffer_1_out | i_o_1__in | or_1_out | RAM_LOAD;  // OR_Gate VAL, 16 bits wide
  assign controlled_buffer_2_out = decoder_1_out25 ? HAS_VALLUE_out : 1'bz;  // Controlled_Buffer controlled_buffer_2
  not not_1 (not_1_out, flags_1_mod);
  assign controlled_buffer_3_out = not_1_out ? OPCODE[23:8] : 16'bz;  // Controlled_Buffer controlled_buffer_3
  or DIV (DIV_out, decoder_1_out4, decoder_1_out5);
  I_O i_o_1 (
    .GET(GET), .OUT_3(decoder_1_out25), .IN(IN), ._IN(i_o_1__in), .PRNT(i_o_1_prnt), .DATA_REG(i_o_1_data_reg));
  REGS regs_1 (
    .CLK(CLK), .RST(RST_out_2), .REG(REG_out), .VAL(VAL_out), .MOV(MOV_out), .RB(regs_1_rb),
    .out_10(regs_1_out_10), .RC(regs_1_rc), .RSI(regs_1_rsi), .SP(regs_1_sp), .PUSH(PSH_out),
    .POP(decoder_1_out29), .RET(decoder_1_out30), .RDI(regs_1_rdi), .RC_2({regs_1_rc_2, GET_2}));
  Pull_Resistor pull_resistor_3 (.node(controlled_buffer_2_out));
  Pull_Resistor pull_resistor_4 (.node(pull_resistor_4_node));
  assign DST_out = pull_resistor_4_node | controlled_buffer_3_out;  // OR_Gate DST, 16 bits wide
  Pull_Resistor pull_resistor_5 (.node(controlled_buffer_3_out));
  Pull_Resistor pull_resistor_6 (.node(pull_resistor_6_node));
  assign controlled_buffer_4_out = i_o_1_prnt ? regs_1_rsi : 16'bz;  // Controlled_Buffer controlled_buffer_4
  assign pull_resistor_6_node = not_2_out ? controlled_buffer_4_out : 16'bz;  // Controlled_Buffer controlled_buffer_5
  not not_2 (not_2_out, controlled_buffer_2_out);
  Pull_Resistor pull_resistor_7 (.node(pull_resistor_7_node));
  assign pull_resistor_7_node = controlled_buffer_2_out ? OPCODE[23:8] : 16'bz;  // Controlled_Buffer controlled_buffer_6
  ALU alu_1 (
    .SOURCE(RAM_STORE), .DEST(DST_out), .ADD(decoder_1_out1), .MUL(SUB_out), .MUL_2(decoder_1_out3),
    .DIV(DIV_out), .SHL(decoder_1_out6), .SHR(decoder_1_out7), .NOT(decoder_1_out9), .AND(decoder_1_out10),
    .OR(decoder_1_out11), .XOR(decoder_1_out8), .CARRY(alu_1_carry), .BORROW(alu_1_borrow),
    .ZERO(alu_1_zero), .OUT(alu_1_out), .MOD(alu_1_mod), .ALU_USED(alu_1_alu_used));
  not not_3 (not_3_out, decoder_1_out12);
  Pull_Resistor pull_resistor_8 (.node(PRNT_DATA));
  assign PRNT_DATA = pull_resistor_6_node | pull_resistor_7_node;  // OR_Gate PRT, 16 bits wide
  and MOV_2 (MOV_2_out, alu_1_alu_used, not_3_out);
  assign controlled_buffer_7_out = decoder_1_out5 ? alu_1_mod : 16'bz;  // Controlled_Buffer controlled_buffer_7
  Pull_Resistor pull_resistor_9 (.node(controlled_buffer_7_out));
  Multiplexer #(.select(3), .width(16), .enable("false")) multiplexer_1 (
    .in0(regs_1_rb), .in1(regs_1_out_10), .in2(regs_1_rc), .in3(regs_1_rsi), .in4(regs_1_rdi),
    .in5(undriven), .in6({regs_1_rc_2, GET_2}), .in7(regs_1_sp), .out(RAM_STORE), .sel(REG_out));
  nor nor_1 (nor_1_out, decoder_1_out15, decoder_1_out16);
  assign controlled_buffer_8_out = nor_1_out ? regs_1_sp : 16'bz;  // Controlled_Buffer controlled_buffer_8
  Multiplexer #(.select(3), .width(16)) multiplexer_2 (
    .in0(regs_1_rb), .in1(regs_1_out_10), .in2(regs_1_rc), .in3(regs_1_rsi), .in4(regs_1_rdi),
    .in5(undriven), .in6({regs_1_rc_2, GET_2}), .in7(regs_1_sp), .out(pull_resistor_4_node),
    .sel(OPCODE[10:8]), .en(flags_1_mod));
  DotMatrix #(.matrixcols(4), .matrixrows(16)) dotmatrix_1 (
    .col0(RAM_STORE), .col1(OPCODE[23:8]), .col2(alu_1_out), .col3(alu_1_mod));
  not not_4 (not_4_out, decoder_1_out5);
  assign controlled_buffer_9_out = not_4_out ? alu_1_out : 16'bz;  // Controlled_Buffer controlled_buffer_9
  Pull_Resistor pull_resistor_10 (.node(controlled_buffer_9_out));
  assign or_1_out = controlled_buffer_7_out | controlled_buffer_9_out;  // OR_Gate or_1, 16 bits wide
  Pull_Resistor pull_resistor_11 (.node(or_1_out));
  or or_2 (OUT, PRNT_DATA[0], PRNT_DATA[1], PRNT_DATA[2], PRNT_DATA[3], PRNT_DATA[4], PRNT_DATA[5], PRNT_DATA[6]);
  not not_5 (not_5_out, nor_1_out);
  assign controlled_buffer_10_out = not_5_out ? regs_1_out_10 : 16'bz;  // Controlled_Buffer controlled_buffer_10
  or or_3 (in_3, decoder_1_out29, decoder_1_out15, decoder_1_out30);
  or or_4 (RAM_LD, PSH_out, decoder_1_out16);
  Pull_Resistor pull_resistor_12 (.node(RAM_STORE));
  Pull_Resistor pull_resistor_13 (.node(controlled_buffer_10_out));
  assign SP = controlled_buffer_10_out | controlled_buffer_8_out;  // OR_Gate or_5, 16 bits wide
  Pull_Resistor pull_resistor_14 (.node(controlled_buffer_8_out));
  // Pins of 1 and 16 bits meet at {regs_1_rc_2, GET_2}

  assign RAM_STR = RAM_LD;

  // Notes on the sheet:
  //   IN: pull=down
  //   RAM_LOAD: pull=down
  //   OPCODE: pull=down
  //   NOP
  //   ADD
  //   SUB
  //   MUL
  //   DIV
  //   MOD
  //   SHL
  //   SHR
  //   XOR
  //   XOR
  //   NOT
  //   AND
  //   OR
  //   TEST
  //   CHDC
  //   CHDR
  //   LOAD
  //   STOR
  //   JMP
  //   JEQ
  //   JNE
  //   JBT
  //   JST
  //   JBE
  //   JLE
  //   GET
  //   OUT
  //   MOV
  //   PUSH
  //   POP
  //   RET
  //   RST
  //   SRC
endmodule

module REGS (
  input  CLK,
  input  RST,
  input  [2:0] REG,
  input  [15:0] VAL,
  input  MOV,
  input  PUSH,
  input  POP,
  input  RET,
  output [15:0] RB,
  output [15:0] out_10,
  output [15:0] RC,
  output [15:0] RSI,
  output [15:0] RDI,
  output [15:0] RC_2,
  output [15:0] SP
);

  wire decoder_1_out0, decoder_1_out1, decoder_1_out2, decoder_1_out3, decoder_1_out4, decoder_1_out5,
       decoder_1_out6, decoder_1_out7, nor_1_out, not_1_out, not_2_out, not_4_out, not_5_out, or_1_out,
       or_5_out, or_7_out;
  wire [2:0] controlled_buffer_3_out, controlled_buffer_4_out, or_4_out;
  wire [15:0] adder_1_out, adder_2_out, controlled_buffer_1_out, controlled_buffer_2_out,
       controlled_buffer_5_out, IP_out, or_2_out, or_6_out, pull_resistor_7_node, pull_resistor_12_node,
       RSI_q, SP_q, subtractor_1_out;

  not not_1 (not_1_out, RET);
  Decoder #(.select(3), .disabled(0)) decoder_1 (
    .out0(decoder_1_out0), .out1(decoder_1_out1), .out2(decoder_1_out2), .out3(decoder_1_out3),
    .out4(decoder_1_out4), .out5(decoder_1_out5), .out6(decoder_1_out6), .out7(decoder_1_out7),
    .sel(or_4_out), .en(or_1_out));
  or or_1 (or_1_out, MOV, POP);
  assign controlled_buffer_1_out = not_1_out ? VAL : 16'bz;  // Controlled_Buffer controlled_buffer_1
  Pull_Resistor pull_resistor_1 (.node(controlled_buffer_1_out));
  assign controlled_buffer_2_out = RET ? adder_1_out : 16'bz;  // Controlled_Buffer controlled_buffer_2
  Adder #(.width(16)) adder_1 (.a(VAL), .b(16'h1), .out(adder_1_out), .cin(1'b0));  // open: cout
  Pull_Resistor pull_resistor_2 (.node(controlled_buffer_2_out));
  assign controlled_buffer_3_out = not_2_out ? REG : 3'bz;  // Controlled_Buffer controlled_buffer_3
  Pull_Resistor pull_resistor_3 (.node(controlled_buffer_3_out));
  not not_2 (not_2_out, PUSH);
  not not_3 (not_2_out, PUSH);
  assign controlled_buffer_4_out = PUSH ? 3'b110 : 3'bz;  // Controlled_Buffer controlled_buffer_4
  Pull_Resistor pull_resistor_4 (.node(controlled_buffer_4_out));
  assign or_2_out = controlled_buffer_1_out | controlled_buffer_2_out;  // OR_Gate or_2, 16 bits wide
  assign or_2_out = controlled_buffer_1_out | controlled_buffer_2_out;  // OR_Gate or_3, 16 bits wide
  Register #(.width(16)) register_1 (.D(or_2_out), .en(decoder_1_out0), .Q(RB), .clk(CLK), .clr(RST));
  Register #(.width(16), .trigger("falling")) RA (.D(or_2_out), .en(decoder_1_out0), .Q(RB), .clk(CLK), .clr(RST));
  assign or_4_out = controlled_buffer_3_out | controlled_buffer_4_out;  // OR_Gate or_4, 3 bits wide
  Register #(.width(16), .max('hffff), .ongoal("stay"), .trigger("falling")) u_RB (
    .D(or_2_out), .en(decoder_1_out1), .Q(out_10), .clk(CLK), .clr(RST));
  Pull_Resistor pull_resistor_5 (.node(RET));
  Register #(.width(16), .trigger("falling")) u_RC (.D(or_2_out), .en(decoder_1_out2), .Q(RC), .clk(CLK), .clr(RST));
  or or_5 (or_5_out, POP, RET);
  Register #(.width(16), .trigger("falling")) u_RDI (.D(or_2_out), .en(decoder_1_out4), .Q(RDI), .clk(CLK), .clr(RST));
  Register #(.width(16), .trigger("falling")) RD (.D(or_2_out), .en(decoder_1_out3), .Q(RSI), .clk(CLK), .clr(RST));
  Register #(.width(16), .trigger("falling")) u_RSI (
    .D(or_2_out), .en(decoder_1_out5), .Q(RSI_q), .clk(CLK), .clr(RST));
  not not_4 (not_4_out, decoder_1_out6);
  Subtractor #(.width(16)) subtractor_1 (.a(SP_q), .b(16'h1), .out(subtractor_1_out), .bin(1'b0));  // open: bout
  Adder #(.width(16)) adder_2 (.a(SP_q), .b(16'h1), .out(adder_2_out), .cin(1'b0));  // open: cout
  Pull_Resistor pull_resistor_6 (.node(RC_2));
  nor nor_1 (nor_1_out, PUSH, or_5_out);
  assign IP_out = PUSH ? subtractor_1_out : 16'bz;  // Controlled_Buffer IP
  assign controlled_buffer_5_out = or_5_out ? adder_2_out : 16'bz;  // Controlled_Buffer controlled_buffer_5
  Pull_Resistor pull_resistor_7 (.node(pull_resistor_7_node));
  assign pull_resistor_7_node = nor_1_out ? or_2_out : 16'bz;  // Controlled_Buffer controlled_buffer_6
  assign or_6_out = pull_resistor_7_node | IP_out | controlled_buffer_5_out;  // OR_Gate or_6, 16 bits wide
  Pull_Resistor pull_resistor_8 (.node(IP_out));
  Pull_Resistor pull_resistor_9 (.node(controlled_buffer_5_out));
  or or_7 (or_7_out, decoder_1_out7, or_5_out, PUSH, RET);
  Pull_Resistor pull_resistor_10 (.node(IP_out));
  Pull_Resistor pull_resistor_11 (.node(controlled_buffer_5_out));
  Pull_Resistor pull_resistor_12 (.node(pull_resistor_12_node));
  assign pull_resistor_12_node = not_5_out ? SP_q : 16'bz;  // Controlled_Buffer controlled_buffer_7
  Register #(.width(16), .trigger("falling")) u_SP (.D(or_6_out), .en(or_7_out), .Q(SP_q), .clk(CLK), .clr(RST));
  not not_5 (not_5_out, PUSH);
  assign SP = pull_resistor_12_node | IP_out;  // OR_Gate or_8, 16 bits wide

  // Notes on the sheet:
  //   CLK: pull=down
  //   PUSH: pull=down
  //   REG: pull=down
  //   MOV: pull=down
  //   RET: pull=down
  //   POP: pull=down
  //   RST: pull=down
endmodule

module FLAGS (
  input  TEST,
  input  CLK,
  input  CLK_2,
  input  JEQ,
  input  JEQ_2,
  input  JNE,
  input  BORROW,
  input  JST,
  input  CARRY,
  input  CARRY_2,
  input  ZERO,
  input  JLE,
  input  JLE_2,
  input  CHDR,
  input  JST_2,
  input  CHDC,
  output MOD,
  output [2:0] IP_REG,
  output JMP_OUT
);

  wire JBE_2_out, JBE_out, JBT_out, JEQ_out, JLE_2_out, JLE_out, JNE_out, JST_out, not_1_out, not_2_out,
       not_3_out, or_1_out, or_2_out, or_4_out, register_1_q, register_3_q, undriven, undriven_2, undriven_3,
       undriven_4;

  not not_1 (not_1_out, register_3_q);
  not not_2 (not_2_out, register_1_q);
  and JBT (JBT_out, not_2_out, undriven_2);
  and u_JST (JST_out, register_1_q, JST);
  not not_3 (not_3_out, register_1_q);
  and JBE (JBE_out, not_3_out, undriven_3);
  and JBE_2 (JBE_2_out, register_1_q, JLE);
  and u_JLE (JLE_out, register_1_q, undriven_3);
  and u_JLE_2 (JLE_2_out, register_1_q, JLE);
  and u_JEQ (JEQ_out, JEQ, register_3_q);
  and u_JNE (JNE_out, JNE, not_1_out);
  or or_1 (or_1_out, JBE_out, JLE_out);
  or or_2 (or_2_out, JBE_2_out, JLE_2_out);
  Pull_Resistor pull_resistor_1 (.node(IP_REG));
  assign IP_REG = JMP_OUT ? 3'b110 : 3'bz;  // Controlled_Buffer controlled_buffer_1
  or or_3 (JMP_OUT, undriven, JEQ_out, JNE_out, JBT_out, JST_out, or_1_out, or_2_out);
  Register #(.width(1), .trigger("falling")) register_1 (
    .D(BORROW), .en(TEST), .Q(register_1_q), .clk(CLK), .clr(undriven_4));
  Register #(.width(1), .trigger("falling")) register_2 (.D(CARRY), .en(TEST), .clk(CLK), .clr(undriven_4));  // open: Q
  Register #(.width(1), .trigger("falling")) register_3 (
    .D(ZERO), .en(TEST), .Q(register_3_q), .clk(CLK), .clr(undriven_4));
  or or_4 (or_4_out, CHDR, CHDC);
  Register #(.width(1), .trigger("falling")) register_4 (.D(CHDR), .en(or_4_out), .Q(MOD), .clk(CLK), .clr(undriven_4));

  assign CARRY_2 = CARRY;
  assign CLK_2 = CLK;
  assign JEQ_2 = JEQ;
  assign JLE_2 = JLE;
  assign JST_2 = CHDR;

  // Notes on the sheet:
  //   JLE: pull=down
  //   JST: pull=down
  //   JEQ: pull=down
  //   CARRY: pull=down
  //   CLK: pull=down
  //   ZERO: pull=down
  //   CHDC: pull=down
  //   JLE_2: pull=down
  //   CHDR: pull=down
  //   TEST: pull=down
  //   JNE: pull=down
  //   JST_2: pull=down
  //   CLK_2: pull=down
  //   MOD: pull=down
  //   CARRY_2: pull=down
  //   BORROW: pull=down
  //   JEQ_2: pull=down
endmodule

module I_O (
  input  [15:0] IN,
  input  GET,
  input  OUT,
  input  OUT_2,
  input  OUT_3,
  output [15:0] _IN,
  output PRNT,
  output [2:0] DATA_REG
);

  assign _IN = GET ? IN : 16'bz;  // Controlled_Buffer controlled_buffer_1
  Pull_Resistor pull_resistor_1 (.node(_IN));
  Pull_Resistor pull_resistor_2 (.node(DATA_REG));
  assign DATA_REG = OUT ? 3'b011 : 3'bz;  // Controlled_Buffer controlled_buffer_2
  Pull_Resistor pull_resistor_3 (.node(DATA_REG));
  Pull_Resistor pull_resistor_4 (.node(DATA_REG));

  assign OUT_2 = OUT;
  assign OUT_3 = OUT;
  assign PRNT = OUT;

  // Notes on the sheet:
  //   OUT: pull=down
  //   IN: pull=down
  //   GET: pull=down
  //   OUT_2: pull=down
  //   OUT_3: pull=down
endmodule
